# Fritzing sketch Untitled Sketch 2 (saved by Fritzing 0.9.3b)

parts:
  元件1 = Arduino Uno (Rev3)
  LED1 = LED - 5mm [color="Red (633nm)" package="5 mm [THT]"]
  元件2 = SRF05 Ultrasonic Rangefinder
  M1 = Dagu DGServo 9g (End View) [part_number=RS001B]

nets:
  N1: 元件1.D8, 元件2.Trig
  N2: 元件1.D9_PWM, 元件2.Echo
  N3: 元件1.D10_PWM/SS, LED1.anode
  GND: 元件1.GND, LED1.cathode, 元件2.GND, M1.gnd
  N4: 元件1.D7, M1.pulse
  3V3: 元件1.3V3, M1.vcc
  5V: 元件1.5V, 元件2.VCC
