# Fritzing sketch Untitled Sketch 2 (saved by Fritzing 0.9.3b)
breadboards: 1

parts:
  DC_Mot_Enc1 = DC Motor with two-phase hall-encoder [part_number=VT-E-G25A-06-177E]
  DC_Mot_Enc2 = DC Motor with two-phase hall-encoder [part_number=VT-E-G25A-06-177E]
  L298N1 = L298N DC motor driver
  元件1 = Arduino Uno (Rev3)

nets:
  N1: DC_Mot_Enc1.pin1, L298N1.OUT4
  GND: DC_Mot_Enc1.pin2, DC_Mot_Enc2.pin2, L298N1.GND, 元件1.GND
  N2: DC_Mot_Enc1.pin3, 元件1.D2
  N3: DC_Mot_Enc1.pin4, 元件1.D12/MISO
  12V: DC_Mot_Enc1.pin5, DC_Mot_Enc2.pin5, L298N1.12V, 元件1.5V
  N4: DC_Mot_Enc1.pin6, L298N1.OUT3
  N5: DC_Mot_Enc2.pin1, L298N1.OUT2
  N6: DC_Mot_Enc2.pin3, 元件1.D3_PWM
  N7: DC_Mot_Enc2.pin4, 元件1.D13/SCK
  N8: DC_Mot_Enc2.pin6, L298N1.OUT1
  N9: L298N1.IN1, 元件1.D10_PWM/SS
  N10: L298N1.IN2, 元件1.D9_PWM
  N11: L298N1.IN3, 元件1.D6_PWM
  N12: L298N1.IN4, 元件1.D5_PWM

custom parts:
  L298N DC motor driver: 2x DC motor driver with 78M05 positive voltage regulator (7..35 V) L298N: max 46 V, 2 A Set 5 V Enable jumper to enable 5 V regultor (needed for the L298N) and +5 V output at screw terminal or supply external +5 V at screw terminal Set ENA and/or ENB to +5 V to enable motor permanently or supply ENA and/or ENB with PWM signal IN1 and IN2 set rotation directory for motor A (OUT1/OUT2) IN2 and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
