# Fritzing sketch 5 (saved by Fritzing 0.9.4)

parts:
  元件1 = Arduino Uno (Rev3)
  M1 = 5-ir-array-sensor [package=THT]

nets:
  N1: 元件1.A0, M1.S5
  N2: 元件1.A1, M1.S4
  N3: 元件1.A2, M1.S3
  N4: 元件1.A3, M1.S2
  N5: 元件1.A4/SDA, M1.S1
  3V3: 元件1.3V3, M1.VCC
  GND: 元件1.GND, M1.GND

custom parts:
  5-ir-array-sensor: 5 IR array sensor.
