# Fritzing sketch 6 (saved by Fritzing 0.9.4)

parts:
  元件1 = Arduino Uno (Rev3)
  元件2 = Bluetooth HC-05 Macho
  LED1 = LED - 5mm [color="Red (633nm)" package="5 mm [THT]"]
  R1 = Resistor [tolerance=±5% resistance=220 package=THT]

nets:
  N1: 元件1.D13/SCK, R1.Pin_1
  GND: 元件1.GND, 元件2.GND, LED1.cathode
  N2: 元件1.D0/RX, 元件2.TXD
  N3: 元件1.D1/TX, 元件2.RXD
  3V3: 元件1.3V3, 元件2.VCC
