# Fritzing sketch 步进电机2 (saved by Fritzing 0.9.4)

parts:
  DRV_1 = DRV 8825 Stepper Motor Carrier, High Current [part_number="DRV 8825"]
  M1 = Stepper Motor - Bipolar
  VCC1 = Battery block 9V
  元件1 = Arduino Mega ADK (Rev3)

nets:
  N1: DRV_1.MS1, 元件1.D8_PWM
  N2: DRV_1.MS2, 元件1.D7_PWM
  N3: DRV_1.MS3, 元件1.D6_PWM
  N4: DRV_1.RESET, 元件1.D5_PWM
  N5: DRV_1.SLEEP, 元件1.D4_PWM
  N6: DRV_1.STEP, 元件1.D3_PWM
  N7: DRV_1.DIRECTION, 元件1.D2_PWM
  N8: DRV_1.VOLTAGE_ST/_MT, VCC1.+
  N9: DRV_1.GROUND_ST/_MT, VCC1.-
  N10: DRV_1.OUT_2B, M1.A
  N11: DRV_1.OUT_2A, M1.C
  N12: DRV_1.OUT_1A, M1.B
  N13: DRV_1.OUT_1B, M1.D
  N14: DRV_1.GROUND_LOG, 元件1.GND
