# Fritzing sketch 步进电机3 (saved by Fritzing 0.9.4)
breadboards: 1

parts:
  元件1 = Arduino Mega ADK (Rev3)
  VCC1 = Battery block 9V
  DRV_1 = DRV 8825 Stepper Motor Carrier, High Current [part_number="DRV 8825"]
  DRV_2 = DRV 8825 Stepper Motor Carrier, High Current [part_number="DRV 8825"]
  M1 = Stepper Motor - Bipolar
  M2 = Stepper Motor - Bipolar

nets:
  N1: 元件1.GND, DRV_1.GROUND_LOG
  N2: 元件1.D11_PWM, DRV_1.RESET
  N3: 元件1.D10_PWM, DRV_1.SLEEP
  N4: 元件1.D9_PWM, DRV_1.STEP
  N5: 元件1.D8_PWM, DRV_1.DIRECTION
  N6: 元件1.D2_PWM, DRV_2.DIRECTION
  N7: 元件1.D3_PWM, DRV_2.STEP
  N8: 元件1.D4_PWM, DRV_2.SLEEP
  N9: 元件1.D5_PWM, DRV_2.RESET
  N10: VCC1.-, DRV_2.GROUND_ST/_MT
  N11: DRV_1.OUT_2B, M2.A
  N12: DRV_1.OUT_2A, M2.C
  N13: DRV_1.OUT_1A, M2.B
  N14: DRV_1.OUT_1B, M2.D
  N15: DRV_2.OUT_2B, M1.A
  N16: DRV_2.OUT_2A, M1.C
  N17: DRV_2.OUT_1A, M1.B
  N18: DRV_2.OUT_1B, M1.D
