# Fritzing sketch CanBus (saved by Fritzing 0.9.4)

parts:
  M1 = Niren can bus module [package=THT]
  元件1 = Arduino Uno (Rev3) - ICSP
  元件2 = Arduino Uno (Rev3) - ICSP
  M2 = Niren can bus module [package=THT]
  LED1 = LED - 5mm [color="Red (633nm)" package="5 mm [THT]"]
  R1 = Resistor [tolerance=±5% resistance=220 package=THT]
  hc-sr1 = hc-sr04

nets:
  N1: M1.pin1, 元件2.5V
  GND: M1.pin2, 元件2.GND, hc-sr1.GND
  N2: M1.pin3, 元件2.D10_PWM/SS
  N3: M1.pin4, 元件2.ICSP_MISO, 元件2.D12/MISO
  N4: M1.pin5, 元件2.ICSP_MOSI, 元件2.D11_PWM/MOSI
  N5: M1.pin6, 元件2.ICSP_SCK, 元件2.D13/SCK
  N6: M1.pin10, M1.pin12, M2.pin12
  N7: M1.pin11, M1.pin13, M2.pin13
  N8: 元件1.ICSP_MOSI, 元件1.D11_PWM/MOSI, M2.pin5
  N9: 元件1.D10_PWM/SS, M2.pin3
  N10: 元件1.D12/MISO, M2.pin4
  N11: 元件1.D13/SCK, M2.pin6
  N12: 元件1.D3_PWM, LED1.cathode
  N13: 元件1.5V, M2.pin1
  N14: 元件1.GND, M2.pin2, R1.Pin_1
  N15: 元件2.D6_PWM, hc-sr1.Echo
  N16: 元件2.D7, hc-sr1.Trig
  3V3: 元件2.3V3, hc-sr1.VCC

custom parts:
  Niren can bus module: Niren can bus module availabe on ebay and others. Pcb view assumes that you unsolder the 7 pin header and resolder it on the bottom of the module to connect to the pcb. The two jumpers and the can bus connector remain on the top of the board and don't appear in pcb view.
