# Fritzing sketch 9 (saved by Fritzing 0.9.4)

parts:
  元件1 = InvenSense MPU6050
  元件2 = Arduino Mega ADK (Rev3)

nets:
  VCC: 元件1.VCC, 元件2.5V
  GND: 元件1.GND, 元件2.GND
  N1: 元件1.SCL, 元件2.D21/SCL
  N2: 元件1.SDA, 元件2.D20/SDA
