# Fritzing sketch 3 (saved by Fritzing 0.9.4)

parts:
  元件1 = Arduino Mega 2560 (Rev3)
  J1 = Basic Servo
  hc-sr1 = hc-sr04
  LED1 = LED - 5mm [color="Red (633nm)" package="5 mm [THT]"]

nets:
  5V: 元件1.5V, hc-sr1.VCC
  GND: 元件1.GND, hc-sr1.GND, LED1.cathode
  N1: 元件1.D50, hc-sr1.Echo
  N2: 元件1.D51, hc-sr1.Trig
  N3: 元件1.D52, LED1.anode
  N4: 元件1.D53, J1.pulse
