# Fritzing sketch 4.1 (saved by Fritzing 0.9.4)

parts:
  L298N1 = L298N DC motor driver
  元件1 = Arduino Mega 2560 (Rev3)
  L298N2 = L298N DC motor driver
  VCC1 = Battery block 9V

nets:
  12V: L298N1.12V, L298N2.12V, VCC1.+
  GND: L298N1.GND, L298N2.GND, VCC1.-
  5V: L298N1.5V, 元件1.5V, L298N2.5V

custom parts:
  L298N DC motor driver: 2x DC motor driver with 78M05 positive voltage regulator (7..35 V) L298N: max 46 V, 2 A Set 5 V Enable jumper to enable 5 V regultor (needed for the L298N) and +5 V output at screw terminal or supply external +5 V at screw terminal Set ENA and/or ENB to +5 V to enable motor permanently or supply ENA and/or ENB with PWM signal IN1 and IN2 set rotation directory for motor A (OUT1/OUT2) IN2 and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
