# Fritzing sketch 4.2 (saved by Fritzing 0.9.4)

parts:
  L298N1 = L298N DC motor driver
  元件1 = Arduino Mega 2560 (Rev3)
  L298N2 = L298N DC motor driver
  M2 = DC Motor  # not connected
  M3 = DC Motor  # not connected
  M4 = DC Motor  # not connected
  M5 = DC Motor  # not connected

nets:
  N1: L298N1.IN1, 元件1.D12_PWM
  N2: L298N1.IN2, 元件1.D11_PWM
  N3: L298N1.IN3, 元件1.D10_PWM
  N4: L298N1.IN4, 元件1.D9_PWM
  N5: 元件1.D8_PWM, L298N2.IN4
  N6: 元件1.D5_PWM, L298N2.ENA, L298N2.IN1
  N7: 元件1.D6_PWM, L298N2.IN2
  N8: 元件1.D7_PWM, L298N2.IN3

custom parts:
  L298N DC motor driver: 2x DC motor driver with 78M05 positive voltage regulator (7..35 V) L298N: max 46 V, 2 A Set 5 V Enable jumper to enable 5 V regultor (needed for the L298N) and +5 V output at screw terminal or supply external +5 V at screw terminal Set ENA and/or ENB to +5 V to enable motor permanently or supply ENA and/or ENB with PWM signal IN1 and IN2 set rotation directory for motor A (OUT1/OUT2) IN2 and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
