# Fritzing sketch 4 (saved by Fritzing 0.9.3b)

parts:
  DC_Mot_Enc1 = DC Motor with two-phase hall-encoder [part_number=VT-E-G25A-06-177E]
  DC_Mot_Enc2 = DC Motor with two-phase hall-encoder [part_number=VT-E-G25A-06-177E]
  L298N1 = L298N DC motor driver
  元件1 = Arduino Mega 2560 (Rev3)
  L298N2 = L298N DC motor driver
  DC_Mot_Enc3 = DC Motor with two-phase hall-encoder [part_number=VT-E-G25A-06-177E]
  DC_Mot_Enc4 = DC Motor with two-phase hall-encoder [part_number=VT-E-G25A-06-177E]
  VCC1 = Battery block 9V

nets:
  N1: DC_Mot_Enc1.pin1, L298N1.OUT4
  N2: DC_Mot_Enc1.pin3, 元件1.D19/RX1
  N3: DC_Mot_Enc1.pin4, 元件1.D43
  N4: DC_Mot_Enc1.pin6, L298N1.OUT3
  N5: DC_Mot_Enc2.pin1, L298N1.OUT2
  N6: DC_Mot_Enc2.pin2, 元件1.GND, DC_Mot_Enc3.pin2
  N7: DC_Mot_Enc2.pin3, 元件1.D18/TX1
  N8: DC_Mot_Enc2.pin4, 元件1.D41
  N9: DC_Mot_Enc2.pin5, 元件1.5V, DC_Mot_Enc3.pin5
  N10: DC_Mot_Enc2.pin6, L298N1.OUT1
  12V: L298N1.12V, L298N2.12V, VCC1.+
  N11: L298N1.GND, VCC1.-
  N12: L298N1.IN1, 元件1.D25
  N13: L298N1.IN2, 元件1.D27
  N14: L298N1.IN3, 元件1.D29
  N15: L298N1.IN4, 元件1.D31
  N16: 元件1.D21/SCL, DC_Mot_Enc4.pin3
  N17: 元件1.D20/SDA, DC_Mot_Enc3.pin3
  N18: 元件1.D33, L298N2.IN1
  N19: 元件1.D35, L298N2.IN2
  N20: 元件1.D37, L298N2.IN3
  N21: 元件1.D39, L298N2.IN4
  N22: 元件1.D45, DC_Mot_Enc4.pin4
  N23: 元件1.D47, DC_Mot_Enc3.pin4
  N24: L298N2.OUT1, DC_Mot_Enc4.pin6
  N25: L298N2.OUT2, DC_Mot_Enc4.pin1
  N26: L298N2.OUT3, DC_Mot_Enc3.pin6
  N27: L298N2.OUT4, DC_Mot_Enc3.pin1

custom parts:
  L298N DC motor driver: 2x DC motor driver with 78M05 positive voltage regulator (7..35 V) L298N: max 46 V, 2 A Set 5 V Enable jumper to enable 5 V regultor (needed for the L298N) and +5 V output at screw terminal or supply external +5 V at screw terminal Set ENA and/or ENB to +5 V to enable motor permanently or supply ENA and/or ENB with PWM signal IN1 and IN2 set rotation directory for motor A (OUT1/OUT2) IN2 and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
