# Fritzing sketch 6 (saved by Fritzing 0.9.4)

parts:
  元件1 = Arduino Mega 2560 (Rev3)
  元件2 = Bluetooth HC-05 Macho
  LED1 = LED - 5mm [color="Red (633nm)" package="5 mm [THT]"]
  R1 = Resistor [tolerance=±5% resistance=220 package=THT]  # not connected

nets:
  N1: 元件1.D15/RX3, 元件2.TXD
  N2: 元件1.D14/TX3, 元件2.RXD
  5V: 元件1.5V, 元件2.VCC
  GND: 元件1.GND, 元件2.GND, LED1.cathode
  N3: 元件1.D52, LED1.anode
