# Fritzing sketch Car (saved by Fritzing 0.9.4)

parts:
  DC_Mot_Enc1 = DC Motor with two-phase hall-encoder [part_number=VT-E-G25A-06-177E]
  DC_Mot_Enc2 = DC Motor with two-phase hall-encoder [part_number=VT-E-G25A-06-177E]
  L298N1 = L298N DC motor driver
  元件1 = Arduino Mega 2560 (Rev3)
  L298N2 = L298N DC motor driver
  DC_Mot_Enc3 = DC Motor with two-phase hall-encoder [part_number=VT-E-G25A-06-177E]
  DC_Mot_Enc4 = DC Motor with two-phase hall-encoder [part_number=VT-E-G25A-06-177E]
  元件2 = Bluetooth HC-05 Macho
  J1 = Basic Servo
  HC-SR04_Sensor_1 = HC-SR04 Ultrasonic Distance Sensor
  M1 = 5-ir-array-sensor [package=THT]
  VCC1 = Battery block 9V

nets:
  N1: DC_Mot_Enc1.pin1, L298N1.OUT4
  N2: DC_Mot_Enc1.pin3, 元件1.D19/RX1
  N3: DC_Mot_Enc1.pin4, 元件1.D43
  N4: DC_Mot_Enc1.pin6, L298N1.OUT3
  N5: DC_Mot_Enc2.pin1, L298N1.OUT2
  GND: DC_Mot_Enc2.pin2, 元件1.GND, HC-SR04_Sensor_1.GND
  N6: DC_Mot_Enc2.pin3, 元件1.D18/TX1
  N7: DC_Mot_Enc2.pin4, 元件1.D41
  5V: DC_Mot_Enc2.pin5, 元件1.5V, HC-SR04_Sensor_1.VCC, HC-SR04_Sensor_1.TRIG
  N8: DC_Mot_Enc2.pin6, L298N1.OUT1
  N9: L298N1.IN1, 元件1.D25
  N10: L298N1.IN2, 元件1.D27
  N11: L298N1.IN3, 元件1.D29
  N12: L298N1.IN4, 元件1.D31
  N13: 元件1.A0, M1.S5
  N14: 元件1.A1, M1.S4
  N15: 元件1.A2, M1.S3
  N16: 元件1.A3, M1.S2
  N17: 元件1.A4, M1.S1
  N18: 元件1.D21/SCL, DC_Mot_Enc4.pin3
  N19: 元件1.D20/SDA, DC_Mot_Enc3.pin3
  N20: 元件1.D15/RX3, 元件2.TXD
  N21: 元件1.D14/TX3, 元件2.RXD
  N22: 元件1.D2_PWM, HC-SR04_Sensor_1.ECHO
  N23: 元件1.D23, J1.pulse
  N24: 元件1.D33, L298N2.IN1
  N25: 元件1.D35, L298N2.IN2
  N26: 元件1.D37, L298N2.IN3
  N27: 元件1.D39, L298N2.IN4
  N28: 元件1.D45, DC_Mot_Enc4.pin4
  N29: 元件1.D47, DC_Mot_Enc3.pin4
  N30: L298N2.OUT1, DC_Mot_Enc4.pin6
  N31: L298N2.OUT2, DC_Mot_Enc4.pin1
  N32: L298N2.OUT3, DC_Mot_Enc3.pin6
  N33: L298N2.OUT4, DC_Mot_Enc3.pin1
  N34: L298N2.12V, VCC1.+
  N35: L298N2.GND, VCC1.-
  GND_2: J1.gnd, M1.GND
  VCC: J1.vcc, M1.VCC

custom parts:
  L298N DC motor driver: 2x DC motor driver with 78M05 positive voltage regulator (7..35 V) L298N: max 46 V, 2 A Set 5 V Enable jumper to enable 5 V regultor (needed for the L298N) and +5 V output at screw terminal or supply external +5 V at screw terminal Set ENA and/or ENB to +5 V to enable motor permanently or supply ENA and/or ENB with PWM signal IN1 and IN2 set rotation directory for motor A (OUT1/OUT2) IN2 and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
  5-ir-array-sensor: 5 IR array sensor.
