# Fritzing sketch Untitled Sketch 2 (saved by Fritzing 0.9.4)

parts:
  DC_Mot_Enc1 = DC Motor with two-phase hall-encoder [part_number=VT-E-G25A-06-177E]
  DC_Mot_Enc2 = DC Motor with two-phase hall-encoder [part_number=VT-E-G25A-06-177E]
  L298N1 = L298N DC motor driver
  元件1 = Arduino Mega 2560 (Rev3)  # not connected
  L298N2 = L298N DC motor driver  # not connected
  DC_Mot_Enc3 = DC Motor with two-phase hall-encoder [part_number=VT-E-G25A-06-177E]  # not connected
  DC_Mot_Enc4 = DC Motor with two-phase hall-encoder [part_number=VT-E-G25A-06-177E]  # not connected
  元件2 = Bluetooth HC-05 Macho  # not connected
  J1 = Basic Servo  # not connected
  HC-SR04_Sensor_1 = HC-SR04 Ultrasonic Distance Sensor  # not connected
  M1 = 5-ir-array-sensor [package=THT]  # not connected

nets:
  N1: DC_Mot_Enc1.pin1, L298N1.OUT4
  N2: DC_Mot_Enc1.pin6, L298N1.OUT3
  N3: DC_Mot_Enc2.pin1, L298N1.OUT2
  N4: DC_Mot_Enc2.pin6, L298N1.OUT1

custom parts:
  L298N DC motor driver: 2x DC motor driver with 78M05 positive voltage regulator (7..35 V) L298N: max 46 V, 2 A Set 5 V Enable jumper to enable 5 V regultor (needed for the L298N) and +5 V output at screw terminal or supply external +5 V at screw terminal Set ENA and/or ENB to +5 V to enable motor permanently or supply ENA and/or ENB with PWM signal IN1 and IN2 set rotation directory for motor A (OUT1/OUT2) IN2 and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
  5-ir-array-sensor: 5 IR array sensor.
