# Fritzing sketch led (saved by Fritzing 0.9.4)

parts:
  元件1 = Arduino Mega 2560 (Rev3)
  LED1 = LED - 5mm [color="Red (633nm)" package="5 mm [THT]"]
  R2 = Resistor [tolerance=±5% resistance=220 package=THT]
  LED2 = smd LED [color="Red (633nm)" package="0805 [SMD]"]
  R3 = Resistor [tolerance=±5% resistance=220 package=THT]

nets:
  N1: 元件1.GND, LED1.cathode, LED2.cathode
  N2: 元件1.D48, R2.Pin_0
  N3: 元件1.D49, R3.Pin_0
